# Fritzing sketch Digital_Temperature_Sensor (saved by Fritzing 0.9.9b)

parts:
  Componente1 = Arduino Uno (Rev3)
  Part1 = KY-028 Digital Temperature Sensor Module [package="Breakout board"]

nets:
  N1: Componente1.A0, Part1.A0
  N2: Componente1.5V, Part1.+
  N3: Componente1.GND, Part1.G

custom parts:
  KY-028 Digital Temperature Sensor Module: KEYES KY-028 Digital Temperature Sensor Module, used to measure changes in temperature.
