# Fritzing sketch water_level_sensor (saved by Fritzing 0.9.9b)

parts:
  Componente1 = Arduino Uno (Rev3)
  Water_Level_Sensor1 = Water Level Sensor [package=board]

nets:
  N1: Componente1.A0, Water_Level_Sensor1.SIG
  5V: Componente1.5V, Water_Level_Sensor1.VCC
  GND: Componente1.GND, Water_Level_Sensor1.GND

custom parts:
  Water Level Sensor: A water level sensor. This sensor operates at 3V to 5V. The Sig (signal) pin outputs an analogue signal that is in proportion to the amount of water in contact with the sensor.
