# Fritzing sketch Flame Sensor (saved by Fritzing 0.9.3b)

parts:
  Componente3 = Arduino Uno (Rev3)
  S1 = KY-026

nets:
  N1: Componente3.A3, S1.pin1
  N2: Componente3.D3_PWM, S1.pin4
  N3: Componente3.5V, S1.pin3
  N4: Componente3.GND, S1.pin2

custom parts:
  KY-026: ky-026 flame sensor module
