# Fritzing sketch Digital_Temperature_Sensor (saved by Fritzing 0.9.9b)

parts:
  Componente1 = Arduino Uno (Rev3)
  ZS-042_RTC1 = ZS-042 RTC Module

nets:
  N1: Componente1.A4/SDA, ZS-042_RTC1.SDA
  N2: Componente1.A5/SCL, ZS-042_RTC1.SCL
  5V: Componente1.5V, ZS-042_RTC1.VCC
  GND: Componente1.GND, ZS-042_RTC1.GND
