# Fritzing sketch servo (saved by Fritzing 0.9.3b)
breadboards: 1

parts:
  Componente1 = Arduino Uno (Rev3)
  R1 = Rotary Potentiometer (Small) [maximum_resistance=100kΩ package=THT]
  J1 = Basic Servo

nets:
  N1: Componente1.A0, R1.wiper
  N2: Componente1.D2, J1.pulse
  3V3: Componente1.3V3, R1.leg1, J1.vcc
  GND: Componente1.GND, R1.leg2, J1.gnd
