# Fritzing sketch Esp32 ejemplo 1 (saved by Fritzing 0.9.3b)
breadboards: 1

parts:
  U1 = ESP32S-HiLetgo [part_number=ESP32S-HiLetgo]
  SW1 = DIP Switch 8 Position [package=dipswitch-08]
  R3 = Resistor [tolerance=±5% power=0.25 resistance=220 package=THT]
  R4 = Rotary Potentiometer (Small) [maximum_resistance=10kΩ package=THT]
  LED1 = LED - 5mm [color="Red (633nm)" current=0.030 package="5 mm [THT]"]
  LED2 = LED - 5mm [color="Red (633nm)" current=0.030 package="5 mm [THT]"]
  LED3 = LED - 5mm [color="Green (555nm)" current=0.030 package="5 mm [THT]"]
  R5 = Resistor [tolerance=±5% power=0.25 resistance=220 package=THT]
  R6 = Resistor [tolerance=±5% power=0.25 resistance=220 package=THT]
  R7 = Resistor [tolerance=±5% resistance=10k package="0402 [SMD]"]
  R8 = Resistor [tolerance=±5% resistance=10k package="0402 [SMD]"]

nets:
  N1: U1.3.3, SW1.1, SW1.3, R4.leg2
  N2: U1.GPIO2, R4.wiper
  N3: U1.GPIO4, LED3.anode
  N4: U1.GPIO19, LED1.anode
  N5: U1.GND, R3.Pin_1, R4.leg1, R5.Pin_1, R6.Pin_1, R7.Pin_1, R8.Pin_1
  N6: U1.GPIO21, LED2.anode
  N7: U1.GPIO22, SW1.16, R8.Pin_0
  N8: U1.GPIO23, SW1.14, R7.Pin_0
  N9: R3.Pin_0, LED3.cathode
  N10: LED1.cathode, R5.Pin_0
  N11: LED2.cathode, R6.Pin_0

custom parts:
  ESP32S-HiLetgo: HiLetgo ESP-WROOM-32 ESP32 ESP-32S Development Board 2.4GHz Dual-Mode WiFi + Bluetooth Dual Cores Microcontroller The ESP32 integrated with Antenna switches, RF Balun, power amplifiers, low-noise amplifiers, filters, and management modules, and the entire solution occupies the least area of PCB. 2.4 GHz Wi-Fi plus Bluetooth dual-mode chip, with TSMC Ultra-low power consumption 40nm technology,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
