# Fritzing sketch LCD display (saved by Fritzing 0.9.3b)
breadboards: 1

parts:
  LCD1 = LCD screen
  Componente1 = Arduino Uno (Rev3) - ICSP
  R4 = Trimmer Potentiometer [maximum_resistance=10kΩ package=THT]

nets:
  VSS: LCD1.VSS, LCD1.R/W, LCD1.LED-, Componente1.GND, R4.leg2
  VDD: LCD1.VDD, LCD1.LED+, Componente1.5V, R4.leg1
  N1: LCD1.V0, R4.wiper
  N2: LCD1.RS, Componente1.D7
  N3: LCD1.E, Componente1.D8
  N4: LCD1.DB4, Componente1.D9_PWM
  N5: LCD1.DB5, Componente1.D10_PWM/SS
  N6: LCD1.DB6, Componente1.D11_PWM/MOSI
  N7: LCD1.DB7, Componente1.D12/MISO
