# Fritzing sketch Temperature and Humidity Module (saved by Fritzing 0.9.3b)

parts:
  Componente1 = Arduino Uno (Rev3) - ICSP
  Part1 = KY-015 Temperature & Humidity Sensor Module [package="Breakout board"]

nets:
  5V: Componente1.5V, Part1.Vin
  N1: Componente1.GND, Part1.-
  N2: Componente1.D8, Part1.S

custom parts:
  KY-015 Temperature & Humidity Sensor Module: DH-11 temperature and humidity sensor in KEYES KY-015 module, provides a low-latency serial interface to measure humidity and temperature.
