# Fritzing sketch Flame SensorModule (saved by Fritzing 0.9.3b)

parts:
  Componente1 = Arduino Uno (Rev3)
  Part1 = KY-026 Flame Sensor Module [package="Breakout board"]

nets:
  N1: Componente1.A3, Part1.A0
  N2: Componente1.D3_PWM, Part1.D0
  N3: Componente1.5V, Part1.+
  N4: Componente1.GND, Part1.G

custom parts:
  KY-026 Flame Sensor Module: KEYES KY-026 Arduino Flame Sensor Module reacts iin the presence of fire.

// code stored in the sketch: Flame SensorModule.ino
int Led = 13 ;// define LED Interface
int buttonpin = 3; // define the flame sensor interface
int analoog = A3; // define the flame sensor interface
int val ;// define numeric variables val
float sensor; //read analoog value
void setup ()
{
pinMode (Led, OUTPUT) ;// define LED as output interface
pinMode (buttonpin, INPUT) ;// output interface defines the flame sensor
pinMode (analoog, INPUT) ;// output interface defines the flame sensor
Serial.begin(9600);
}
void loop ()
{
sensor = analogRead(analoog);
Serial.println(sensor); // display tempature
val = digitalRead (buttonpin) ;// digital interface will be assigned a value of 3 to read
val
if (val == HIGH) // When the flame sensor detects a signal, LED flashes
{

digitalWrite (Led, HIGH);
}
else
{
digitalWrite (Led, LOW);
}
delay(1000);
