# Fritzing sketch Photo-InterrupterModule (saved by Fritzing 0.9.3b)

parts:
  Componente1 = Arduino Uno (Rev3)
  Part1 = KY-010 Photo Interrupter Module [package="Breakout board"]

nets:
  N1: Componente1.D3_PWM, Part1.-
  5V: Componente1.5V, Part1.Vin
  N2: Componente1.GND, Part1.S

custom parts:
  KY-010 Photo Interrupter Module: Photo Interrupter Module Keyes KY-010 for Arduino, will trigger a signal when light between the sensor's gap is blocked.

// code stored in the sketch: Photo-InterrupterModule.ino
int Led=13;
int sensor=3;
int val;
void setup()
{
pinMode(Led,OUTPUT);
pinMode(sensor,INPUT);
}
void loop()

3 / 3

{
val=digitalRead(sensor);
if(val==HIGH)
{
digitalWrite(Led,HIGH);
}
else
{
digitalWrite(Led,LOW);
}

}
