# Fritzing sketch Reed Switch Module (saved by Fritzing 0.9.3b)

parts:
  Componente1 = Arduino Uno (Rev3)
  Part1 = KY-025 Reed Switch Module [package="Breakout board"]

nets:
  N1: Componente1.D3_PWM, Part1.D0
  N2: Componente1.5V, Part1.+
  N3: Componente1.GND, Part1.G

custom parts:
  KY-025 Reed Switch Module: KEYES KY-025 Arduino Reed Switch Module reacts iin the presence of a magnetic field.

// code stored in the sketch: Reed Switch Module.ino
int Led = 13 ; // define LED Interface
int Sensor = 3; // define the Reed sensor interfaces
int val; // define numeric variables val
void setup ()
{

pinMode (Led, OUTPUT) ; // define LED as output interface
pinMode (Sensor, INPUT) ; // output interface as defined Reed sensor

}
void loop ()
{
val = digitalRead (Sensor) ; // digital interface will be assigned a value of 3 to read val

3 / 3

if (val == HIGH) // When the Reed sensor detects a signal, LED flashes
{
digitalWrite (Led, HIGH);
}
else
{
digitalWrite (Led, LOW);
}
}
