# Fritzing sketch circuito5 (saved by Fritzing 0.9.3b)
breadboards: 1

parts:
  U1 = ESP32S-HiLetgo [part_number=ESP32S-HiLetgo]
  R1 = Resistor [tolerance=±5% resistance=10 package=THT]
  LED1 = LED - 5mm [color="Red (633nm)" package="5 mm [THT]"]
  LED2 = LED - 5mm [color="Red (633nm)" package="5 mm [THT]"]
  LED3 = LED - 5mm [color="Green (555nm)" package="5 mm [THT]"]
  R6 = Resistor [tolerance=±5% resistance=220 package=THT]
  R7 = Rotary Potentiometer (Small) [maximum_resistance=100kΩ package=THT]
  SW1 = DIP Switch 8 Position [package=dipswitch-08]
  R3 = Resistor [tolerance=±5% resistance=10 package=THT]
  R9 = Resistor [tolerance=±5% resistance=220 package=THT]
  R11 = Resistor [tolerance=±5% resistance=220 package=THT]

nets:
  N1: U1.3.3, R7.leg2, SW1.1, SW1.3
  N2: U1.GND, R1.Pin_1, R6.Pin_1, R7.leg1, R3.Pin_0, R9.Pin_1, R11.Pin_1
  N3: U1.GPIO2, R7.wiper
  N4: U1.GPIO4, LED3.anode
  N5: U1.GPIO19, LED1.anode
  N6: U1.GPIO21, LED2.anode
  N7: U1.GPIO22, R1.Pin_0, SW1.16
  N8: U1.GPIO23, SW1.14, R3.Pin_1
  N9: LED1.cathode, LED3.cathode, R6.Pin_0, R11.Pin_0
  N10: LED2.cathode, R9.Pin_0

custom parts:
  ESP32S-HiLetgo: HiLetgo ESP-WROOM-32 ESP32 ESP-32S Development Board 2.4GHz Dual-Mode WiFi + Bluetooth Dual Cores Microcontroller The ESP32 integrated with Antenna switches, RF Balun, power amplifiers, low-noise amplifiers, filters, and management modules, and the entire solution occupies the least area of PCB. 2.4 GHz Wi-Fi plus Bluetooth dual-mode chip, with TSMC Ultra-low power consumption 40nm technology,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
