# Fritzing sketch blink_esp8266 (saved by Fritzing 0.9.9b)
breadboards: 1

parts:
  U1 = NodeMCU V3.0
  R1 = Resistor [tolerance=±5% power=0.25 resistance=220 package=THT]
  LED1 = LED - 5mm [color="Red (633nm)" current=0.030 package="5 mm [THT]"]

nets:
  N1: U1.GND, LED1.cathode
  N2: U1.D5, R1.Pin_0
  N3: R1.Pin_1, LED1.anode

custom parts:
  NodeMCU V3.0: NodeMcu V3 Lua WIFI Development Board
