# Fritzing sketch button_esp8266 (saved by Fritzing 0.9.9b)

parts:
  U1 = NodeMCU V3.0
  Grove1 = Grove Button
  Grove_LED_Red1 = Grove LED Red

nets:
  N1: U1.D1, Grove_LED_Red1.SIG
  GND: U1.GND, Grove1.GND, Grove_LED_Red1.GND
  N2: U1.D6, Grove1.SIG

custom parts:
  NodeMCU V3.0: NodeMcu V3 Lua WIFI Development Board
  Grove LED Red: LED red, Grove connector.
