# Fritzing sketch fading_esp8266 (saved by Fritzing 0.9.9b)

parts:
  U1 = NodeMCU V3.0
  Grove_LED_Red1 = Grove LED Red

nets:
  N1: U1.D2, Grove_LED_Red1.SIG
  GND: U1.GND, Grove_LED_Red1.GND

custom parts:
  NodeMCU V3.0: NodeMcu V3 Lua WIFI Development Board
  Grove LED Red: LED red, Grove connector.
