# Fritzing sketch rotary_encorder-ESP32 (saved by Fritzing 0.9.9b)

parts:
  U1 = ESP32S-HiLetgo [part_number=ESP32S-HiLetgo]
  RE1 = KY-040 Rotary encoder [package=THT]

nets:
  N1: U1.3.3, RE1.Vcc
  N2: U1.GPIO14, RE1.CLK
  N3: U1.GPIO12, RE1.DT
  GND: U1.GND, RE1.GND
  N4: U1.GPIO13, RE1.SW

custom parts:
  ESP32S-HiLetgo: HiLetgo ESP-WROOM-32 ESP32 ESP-32S Development Board 2.4GHz Dual-Mode WiFi + Bluetooth Dual Cores Microcontroller The ESP32 integrated with Antenna switches, RF Balun, power amplifiers, low-noise amplifiers, filters, and management modules, and the entire solution occupies the least area of PCB. 2.4 GHz Wi-Fi plus Bluetooth dual-mode chip, with TSMC Ultra-low power consumption 40nm technology,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
  KY-040 Rotary encoder: KY-040 Rotary Encoder with switch on breakout borad from AZ Delivery
